// Logisim project a.circ as structural Verilog: 8 circuits, main circuit main
module main (
  output [7:0] out_1,
  output [7:0] out_2
);

  AddMachine addmachine_1 (.Oadd(out_1), .Oreg(out_2));
endmodule

module NAND (
  input  in_1,
  input  in_2,
  output out_3
);

  wire and_1_out;

  and and_1 (and_1_out, in_1, in_2);
  not not_1 (out_3, and_1_out);
endmodule

module NOR (
  input  in_1,
  input  in_2,
  output out_3
);

  wire or_1_out;

  not not_1 (out_3, or_1_out);
  or or_1 (or_1_out, in_1, in_2);
endmodule

module _2_to_1_MUX (
  input  a,
  input  b,
  input  s,
  output out_4
);

  wire and_1_out, and_2_out, not_1_out;

  not not_1 (not_1_out, s);
  and and_1 (and_1_out, not_1_out, a);
  and and_2 (and_2_out, s, b);
  or or_1 (out_4, and_1_out, and_2_out);
endmodule

module _4_to_1_MUX (
  input  I0,
  input  I2,
  input  I1,
  input  I4,
  input  s0,
  input  s1,
  output out_7
);

  wire n2_to_1_mux_1_out_4, n2_to_1_mux_3_out_4;

  _2_to_1_MUX u_2_to_1_mux_1 (.a(I0), .b(I2), .s(s0), .out_4(n2_to_1_mux_1_out_4));
  _2_to_1_MUX u_2_to_1_mux_2 (.a(n2_to_1_mux_1_out_4), .b(n2_to_1_mux_3_out_4), .s(s1), .out_4(out_7));
  _2_to_1_MUX u_2_to_1_mux_3 (.a(I1), .b(I4), .s(s0), .out_4(n2_to_1_mux_3_out_4));
endmodule

module AddMachine (
  output [7:0] Oadd,
  output [7:0] Oreg
);

  wire clock_1_out;

  Adder adder_1 (.a(8'h1), .b(Oreg), .out(Oadd));  // open: cin, cout
  Register register_1 (.D(Oadd), .Q(Oreg), .clk(clock_1_out));  // open: en, clr
  Clock clock_1 (.out(clock_1_out));
endmodule

module XOR (
  input  in_1,
  input  in_2,
  output out_3
);

  wire and_1_out, not_1_out, or_1_out;

  and and_1 (and_1_out, in_1, in_2);
  or or_1 (or_1_out, in_1, in_2);
  not not_1 (not_1_out, and_1_out);
  and and_2 (out_3, or_1_out, not_1_out);
endmodule

module _4_to_1_MUX2 (
  input  I0,
  input  I2,
  input  I1,
  input  I4,
  input  s0,
  input  s1,
  output x
);

  wire and_1_out, and_2_out, and_3_out, and_4_out, not_1_out, not_2_out, not_3_out, not_4_out;

  not not_1 (not_1_out, s0);
  not not_2 (not_2_out, s1);
  not not_3 (not_3_out, s0);
  not not_4 (not_4_out, s1);
  and and_1 (and_1_out, I4, s0, s1);
  and and_2 (and_2_out, I1, not_1_out, s1);
  and and_3 (and_3_out, I2, s0, not_2_out);
  and and_4 (and_4_out, I0, not_3_out, not_4_out);
  or or_1 (x, and_1_out, and_2_out, and_3_out, and_4_out);
endmodule
