// Logisim project part1.circ as structural Verilog: 2 circuits, main circuit main
module main (
  input  in_1,
  input  in_2,
  output out_3
);

  NAND nand_1 (.in_1(in_1), .in_2(in_2), .out_3(out_3));
endmodule

module NAND (
  input  in_1,
  input  in_2,
  output out_3
);

  wire and_1_out;

  and and_1 (and_1_out, in_1, in_2);
  not not_1 (out_3, and_1_out);
endmodule
