// Logisim project Part A.circ as structural Verilog
module Splitters (
  input  [7:0] In,
  output Out1,
  output [7:0] Out2
);

  not not_1 (Out2[7], In[7]);
  and and_1 (Out1, In[0], In[7]);

  assign Out2[6:0] = In[6:0];
endmodule

module Rotate_Right (
  input  [3:0] in_1,
  input  [15:0] \input ,
  output [15:0] out_3
);

  wire [15:0] rotr2_1_out_3, rotr4_1_out_3, rotr8_1_out_3;

  rotr8 rotr8_1 (.in_2(\input ), .in_1(in_1[3]), .out_3(rotr8_1_out_3));
  rotr4 rotr4_1 (.in_2(rotr8_1_out_3), .in_1(in_1[2]), .out_3(rotr4_1_out_3));
  rotr2 rotr2_1 (.in_2(rotr4_1_out_3), .in_1(in_1[1]), .out_3(rotr2_1_out_3));
  rotr1 rotr1_1 (.\input (rotr2_1_out_3), .select(in_1[0]), .out_3(out_3));
endmodule

module rotr1 (
  input  select,
  input  [15:0] \input ,
  output [15:0] out_3
);

  Multiplexer #(.width(16), .enable("false")) multiplexer_1 (
    .in0(\input ), .in1({\input [0], \input [15:1]}), .out(out_3), .sel(select));
endmodule

module rotr2 (
  input  in_1,
  input  [15:0] in_2,
  output [15:0] out_3
);

  wire [15:0] rotr1_1_out_3;

  rotr1 rotr1_1 (.\input (in_2), .select(in_1), .out_3(rotr1_1_out_3));
  rotr1 rotr1_2 (.\input (rotr1_1_out_3), .select(in_1), .out_3(out_3));
endmodule

module rotr4 (
  input  in_1,
  input  [15:0] in_2,
  output [15:0] out_3
);

  wire [15:0] rotr2_1_out_3;

  rotr2 rotr2_1 (.in_2(in_2), .in_1(in_1), .out_3(rotr2_1_out_3));
  rotr2 rotr2_2 (.in_2(rotr2_1_out_3), .in_1(in_1), .out_3(out_3));
endmodule

module rotr8 (
  input  in_1,
  input  [15:0] in_2,
  output [15:0] out_3
);

  wire [15:0] rotr4_1_out_3;

  rotr4 rotr4_1 (.in_2(in_2), .in_1(in_1), .out_3(rotr4_1_out_3));
  rotr4 rotr4_2 (.in_2(rotr4_1_out_3), .in_1(in_1), .out_3(out_3));
endmodule
