// Logisim project lab6ALU.circ as structural Verilog: 1 circuit, main circuit ALU
// LAB12-ALU
module ALU (
  input  [31:0] ALU_Source_1,
  input  [31:0] ALU_Source_2,
  input  [2:0] ALU_Control,
  output [31:0] ALU_Result
);

  wire [4:0] bit_extender_1_out, bit_extender_2_out, bit_extender_3_out, bit_extender_4_out,
       bit_extender_5_out;
  wire [31:0] \and , \or , rotl, rotr, sla, sll, srl, \xor ;

  // Probe on ALU_Source_1
  // Probe on ALU_Source_2
  Bit_Extender #(.in_width(32), .out_width(5)) bit_extender_1 (.in(ALU_Source_2), .out(bit_extender_1_out));
  Bit_Extender #(.in_width(32), .out_width(5)) bit_extender_2 (.in(ALU_Source_2), .out(bit_extender_2_out));
  Bit_Extender #(.in_width(32), .out_width(5)) bit_extender_3 (.in(ALU_Source_2), .out(bit_extender_3_out));
  Bit_Extender #(.in_width(32), .out_width(5)) bit_extender_4 (.in(ALU_Source_2), .out(bit_extender_4_out));
  Bit_Extender #(.in_width(32), .out_width(5)) bit_extender_5 (.in(ALU_Source_2), .out(bit_extender_5_out));
  Shifter #(.width(32)) shifter_1 (.in(ALU_Source_1), .\dist (bit_extender_1_out), .out(sll));
  Shifter #(.width(32), .shift("lr")) shifter_2 (.in(ALU_Source_1), .\dist (bit_extender_2_out), .out(srl));
  Shifter #(.width(32), .shift("ar")) shifter_3 (.in(ALU_Source_1), .\dist (bit_extender_3_out), .out(sla));
  Shifter #(.width(32), .shift("rl")) shifter_4 (.in(ALU_Source_1), .\dist (bit_extender_4_out), .out(rotl));
  Shifter #(.width(32), .shift("rr")) shifter_5 (.in(ALU_Source_1), .\dist (bit_extender_5_out), .out(rotr));
  assign \and  = ALU_Source_1 & ALU_Source_2;  // AND_Gate and_1, 32 bits wide
  assign \or  = ALU_Source_1 | ALU_Source_2;  // OR_Gate or_1, 32 bits wide
  assign \xor  = ALU_Source_1 ^ ALU_Source_2;  // XOR_Gate xor_1, 32 bits wide
  Multiplexer #(.select(3), .width(32), .enable("false")) multiplexer_1 (
    .in0(sll), .in1(srl), .in2(sla), .in3(rotl), .in4(rotr), .in5(\and ), .in6(\or ), .in7(\xor ),
    .out(ALU_Result), .sel(ALU_Control));
  // Probe on ALU_Result

  // Other names for the same wires on the sheet: control[2:0] = ALU_Control; result[31:0] = ALU_Result;
  //   source1[31:0] = ALU_Source_1; source2[31:0] = ALU_Source_2

  // Notes on the sheet:
  //   DO NOT CROSS WIRES
  //   OVER THIS BOX
  //   DO NOT CROSS WIRES
  //   OVER THIS BOX
  //   COMPUTE ALL POSSIBLE OPERATIONS
  //   * YOUR CIRCUIT HERE *
  //   DO NOT CROSS WIRES
  //   OVER THIS BOX
  //   DO NOT CROSS WIRES
  //   OVER THIS BOX
  //   SELECT THE REQUESTED RESULT
  //   * YOUR CIRCUIT HERE *
  //   DO NOT CROSS WIRES
  //   OVER THIS BOX
endmodule
