// Logisim project MultRepeatedAdder.circ as structural Verilog: 3 circuits, main circuit main
module main (
  input  [31:0] Input_A,
  input  [31:0] Input_B,
  input  Reset,
  output [31:0] Product,
  output Stall_Pipeline
);

  wire Clock_out;

  Clock Clock (.out(Clock_out));
  // Probe on Input_B
  // Probe on Input_A
  // Probe on Product
  Mult mult_1 (
    .A(Input_A), .B(Input_B), .Clock(Clock_out), .Reset(Reset), .Product(Product),
    .Stall_Pipeline(Stall_Pipeline));
endmodule

module Mult (
  input  [31:0] A,
  input  [31:0] B,
  input  Clock,
  input  Reset,
  output [31:0] Product,
  output Stall_Pipeline
);

  wire [31:0] register_1_q, register_2_q, register_3_q;

  // Probe on A
  // Probe on B
  // Probe on register_1_q
  Register #(.width(32)) register_1 (.D(A), .en(Reset), .Q(register_1_q), .clk(Clock));  // open: clr
  // Probe on register_3_q
  Register #(.width(32)) register_2 (.D(B), .en(Reset), .Q(register_2_q), .clk(Clock));  // open: clr
  // Probe on register_2_q
  Adder #(.width(32)) adder_1 (.a(register_1_q), .b(register_3_q), .out(Product));  // open: cin, cout
  // Probe on Product
  Register #(.width(32)) register_3 (.D(Product), .en(Stall_Pipeline), .Q(register_3_q), .clk(Clock));  // open: clr
  CountUpTo countupto_1 (.Reset(Reset), .Limit(register_2_q), .IsCounting(Stall_Pipeline), .Clock(Clock));
  // Probe on Stall_Pipeline

  // Other names for the same wires on the sheet: clk = Clock; isCounting = Stall_Pipeline;
  //   shouldStall = Stall_Pipeline

  // Notes on the sheet:
  //   INPUTS
  //   IMPLEMENT A*B
  //   OUTPUTS
endmodule

module CountUpTo (
  input  Reset,
  input  Clock,
  input  [31:0] Limit,
  output IsCounting
);

  wire comparator_1_eq;
  wire [31:0] counter_1_q, subtractor_1_out;

  Counter #(.width(32), .max('hffffffff)) counter_1 (
    .load(1'b0), .count(IsCounting), .Q(counter_1_q), .clk(Clock), .clr(Reset));  // open: D, carry
  Subtractor #(.width(32)) subtractor_1 (.a(Limit), .b(32'h1), .out(subtractor_1_out));  // open: bin, bout
  Comparator #(.width(32)) comparator_1 (.a(counter_1_q), .b(subtractor_1_out), .eq(comparator_1_eq));  // open: gt, lt
  not not_1 (IsCounting, comparator_1_eq);

  // Other names for the same wires on the sheet: clk = Clock; rst = Reset

  // Notes on the sheet:
  //   INPUTS
  //   IMPLEMENT
  //   OUTPUTS
endmodule
