// Logisim project fib_solution.circ as structural Verilog: 3 circuits, main circuit main
module main (
  input  [3:0] in_1,
  output [9:0] out_2
);

  wire clock_1_out, continue_signal;
  wire [7:0] counter_1_q;
  wire [9:0] fib_i, fib_i_1_q, init_1_out_2;

  // Probe on fib_i
  init init_1 (.in_1(out_2), .out_2(init_1_out_2));
  Register #(.width(10)) fib_i_1 (.D(fib_i), .en(continue_signal), .Q(fib_i_1_q), .clk(clock_1_out));  // open: clr
  // Probe on init_1_out_2
  Register #(.width(10)) fib_i_3 (.D(init_1_out_2), .en(continue_signal), .Q(fib_i), .clk(clock_1_out));  // open: clr
  Clock clock_1 (.out(clock_1_out));
  // Probe on fib_i_1_q
  Adder #(.width(10)) adder_1 (.a(fib_i_1_q), .b(fib_i), .out(out_2));  // open: cin, cout
  // Probe on fib_i
  halt halt_1 (.input_N(in_1), .CLK(clock_1_out), .continue_signal(continue_signal));
  Counter counter_1 (.load(1'b0), .count(1'b1), .Q(counter_1_q), .clk(clock_1_out));  // open: D, carry, clr
  // Probe on counter_1_q
  // Probe on out_2

  // Other names for the same wires on the sheet: fib_i_1[9:0] = out_2; input_N[3:0] = in_1
endmodule

module halt (
  input  [3:0] input_N,
  input  CLK,
  output continue_signal
);

  wire comparator_1_eq, not_1_out;
  wire [3:0] adder_1_out, counter_1_q;

  // Probe on not_1_out
  not not_1 (not_1_out, comparator_1_eq);
  // Probe on counter_1_q
  Counter #(.width(4), .max('hf)) counter_1 (
    .load(1'b0), .count(not_1_out), .Q(counter_1_q), .clk(CLK));  // open: D, carry, clr
  Adder #(.width(4)) adder_1 (.a(counter_1_q), .b(4'b0001), .out(adder_1_out));  // open: cin, cout
  // Probe on adder_1_out
  Comparator #(.width(4), .mode("unsigned")) comparator_1 (
    .a(input_N), .b(adder_1_out), .eq(comparator_1_eq));  // open: gt, lt
  not not_2 (continue_signal, comparator_1_eq);
endmodule

module init (
  input  [9:0] in_1,
  output [9:0] out_2
);

  wire comparator_1_eq;

  Comparator #(.width(10)) comparator_1 (.a(in_1), .b({10{1'b0}}), .eq(comparator_1_eq));  // open: gt, lt
  Multiplexer #(.width(10), .enable("false")) multiplexer_1 (
    .in0(in_1), .in1(10'h1), .out(out_2), .sel(comparator_1_eq));
endmodule
