// Logisim project pipeline.circ as structural Verilog: 3 circuits, main circuit main
module main (
  output [7:0] Non_pipelined_Out,
  output [7:0] Pipelined_Out
);

  wire CLK_out;
  wire [7:0] Address_Counter_q, rom_1_data;

  Clock CLK (.out(CLK_out));
  Counter Address_Counter (.Q(Address_Counter_q), .clk(CLK_out));  // open: load, D, count, carry, clr
  ROM rom_1 (.addr(Address_Counter_q), .data(rom_1_data));  // open: sel
  Non_pipelined Non_pipelined (.In2(8'h1), .In3(rom_1_data), .CLK(CLK_out), .Non_pipelined_Out(Non_pipelined_Out));
  Pipelined Pipelined (.In2(8'h1), .In3(rom_1_data), .CLK(CLK_out), .Pipelined_Out(Pipelined_Out));
  // Probe on Non_pipelined_Out
  // Probe on Pipelined_Out

  // Notes on the sheet:
  //   contents of rom_1 (hex, n*v repeats v):
  //   3 2 fc 1 2 fb 1
endmodule

module Non_pipelined (
  input  [7:0] In2,
  input  [7:0] In3,
  input  CLK,
  output [7:0] Non_pipelined_Out
);

  wire [7:0] adder_1_out, multiplier_1_out;

  Multiplier multiplier_1 (.a(In2), .b(In3), .out(multiplier_1_out));  // open: cin, cout
  Adder adder_1 (.a(multiplier_1_out), .b(Non_pipelined_Out), .out(adder_1_out));  // open: cin, cout
  Register N_p_Reg (.D(adder_1_out), .Q(Non_pipelined_Out), .clk(CLK));  // open: en, clr
endmodule

module Pipelined (
  input  [7:0] In2,
  input  [7:0] In3,
  input  CLK,
  output [7:0] Pipelined_Out
);

  wire [7:0] adder_1_out, mul_Reg_q, multiplier_1_out;

  // Probe on In2
  // Probe on In3
  // Probe on multiplier_1_out
  Multiplier multiplier_1 (.a(In2), .b(In3), .out(multiplier_1_out));  // open: cin, cout
  // Probe on mul_Reg_q
  Register mul_Reg (.D(multiplier_1_out), .Q(mul_Reg_q), .clk(CLK));  // open: en, clr
  // Probe on adder_1_out
  Adder adder_1 (.a(mul_Reg_q), .b(Pipelined_Out), .out(adder_1_out));  // open: cin, cout
  // Probe on Pipelined_Out
  Register add__Reg (.D(adder_1_out), .Q(Pipelined_Out), .clk(CLK));  // open: en, clr
endmodule
